// Logisim project control_logic.circ as structural Verilog: 1 circuit, main circuit control_logic
module control_logic (
  input  [31:0] inst,
  input  BrEq,
  input  BrLt,
  output PCSel,
  output RegWEn,
  output [2:0] ImmSel,
  output BrUn,
  output ASel,
  output BSel,
  output [3:0] ALUSel,
  output MemRW,
  output [1:0] WBSel,
  output CSRSel,
  output CSRWen,
  output [3:0] WSel,
  output [3:0] RSel
);

  wire a00, a01, a02, a03, a04, a05, a06, a07, a10, a11, a12, a14, and_2_out, and_3_out, and_4_out,
       and_5_out, and_6_out, and_7_out, and_8_out, and_13_out, and_19_out, and_24_out, and_25_out,
       and_26_out, and_27_out, and_28_out, and_29_out, comparator_1_eq, comparator_2_eq, comparator_3_eq,
       comparator_4_eq, comparator_5_eq, comparator_6_eq, comparator_7_eq, comparator_8_eq, comparator_9_eq,
       comparator_10_eq, comparator_11_eq, comparator_12_eq, comparator_13_eq, comparator_14_eq,
       comparator_15_eq, comparator_16_eq, comparator_17_eq, comparator_18_eq, comparator_19_eq,
       comparator_20_eq, comparator_21_eq, comparator_22_eq, comparator_23_eq, comparator_24_eq,
       comparator_25_eq, comparator_26_eq, comparator_27_eq, comparator_28_eq, comparator_29_eq,
       comparator_30_eq, comparator_31_eq, comparator_32_eq, comparator_33_eq, comparator_34_eq,
       comparator_35_eq, comparator_36_eq, comparator_37_eq, comparator_38_eq, comparator_39_eq,
       comparator_40_eq, comparator_41_eq, comparator_42_eq, comparator_43_eq, comparator_44_eq,
       comparator_45_eq, comparator_46_eq, comparator_47_eq, comparator_48_eq, comparator_49_eq,
       comparator_50_eq, comparator_52_eq, comparator_53_eq, comparator_55_eq, comparator_56_eq,
       comparator_57_eq, comparator_58_eq, comparator_59_eq, comparator_60_eq, comparator_61_eq,
       comparator_62_eq, comparator_63_eq, comparator_64_eq, comparator_65_eq, decoder_1_out0,
       decoder_1_out1, decoder_1_out4, decoder_1_out5, decoder_1_out6, decoder_1_out7, not_1_out, not_2_out,
       not_3_out, not_4_out, not_6_out, not_7_out, not_8_out, or_1_out, or_2_out, or_3_out, or_4_out,
       or_7_out, or_9_out, or_10_out, or_11_out, or_12_out, or_13_out, or_14_out, or_15_out, or_16_out,
       or_17_out, or_18_out, or_20_out, or_21_out, or_22_out, or_23_out, or_24_out;

  Comparator #(.width(7)) comparator_1 (.a(inst[6:0]), .b(7'b1100111), .eq(comparator_1_eq));  // open: gt, lt
  Comparator #(.width(7)) comparator_2 (.a(inst[6:0]), .b(7'b1101111), .eq(comparator_2_eq));  // open: gt, lt
  and and_1 (a14, comparator_18_eq, comparator_15_eq, comparator_16_eq);
  Decoder #(.enable("false"), .select(3)) decoder_1 (
    .out0(decoder_1_out0), .out1(decoder_1_out1), .out4(decoder_1_out4), .out5(decoder_1_out5),
    .out6(decoder_1_out6), .out7(decoder_1_out7), .sel(inst[14:12]));  // open: out2, out3
  Comparator #(.width(7)) comparator_3 (.a(inst[6:0]), .b(7'b1100011), .eq(comparator_3_eq));  // open: gt, lt
  Comparator #(.width(7)) comparator_4 (.a(inst[6:0]), .b(7'b1100111), .eq(comparator_4_eq));  // open: gt, lt
  Comparator #(.width(7)) comparator_5 (.a(inst[6:0]), .b(7'b1101111), .eq(comparator_5_eq));  // open: gt, lt
  Comparator #(.width(7)) comparator_6 (.a(inst[6:0]), .b(7'b0110011), .eq(comparator_6_eq));  // open: gt, lt
  Comparator #(.width(7)) comparator_7 (.a(inst[6:0]), .b(7'b0000011), .eq(comparator_7_eq));  // open: gt, lt
  Comparator #(.width(7)) comparator_8 (.a(inst[6:0]), .b(7'b0010011), .eq(comparator_8_eq));  // open: gt, lt
  Comparator #(.width(7)) comparator_9 (.a(inst[6:0]), .b(7'b0010111), .eq(comparator_9_eq));  // open: gt, lt
  Comparator #(.width(3)) comparator_10 (.a(inst[14:12]), .b(3'b000), .eq(comparator_10_eq));  // open: gt, lt
  Comparator #(.width(7)) comparator_11 (.a(inst[6:0]), .b(7'b0110011), .eq(comparator_11_eq));  // open: gt, lt
  Comparator #(.width(7)) comparator_12 (.a(inst[6:0]), .b(7'b0010011), .eq(comparator_12_eq));  // open: gt, lt
  Comparator #(.width(7)) comparator_13 (.a(inst[6:0]), .b(7'b0000011), .eq(comparator_13_eq));  // open: gt, lt
  Comparator #(.width(7)) comparator_14 (.a(inst[6:0]), .b(7'b0100011), .eq(comparator_14_eq));  // open: gt, lt
  or or_1 (or_1_out, comparator_1_eq, comparator_2_eq);
  Comparator #(.width(7)) comparator_15 (.a(inst[6:0]), .b(7'b0110011), .eq(comparator_15_eq));  // open: gt, lt
  Comparator #(.width(7)) comparator_16 (.a(inst[31:25]), .b(7'b0000001), .eq(comparator_16_eq));  // open: gt, lt
  Comparator #(.width(7)) comparator_17 (.a(inst[31:25]), .b(7'b0100000), .eq(comparator_17_eq));  // open: gt, lt
  Comparator #(.width(3)) comparator_18 (.a(inst[14:12]), .b(3'b001), .eq(comparator_18_eq));  // open: gt, lt
  and and_2 (and_2_out, BrEq, decoder_1_out0);
  not not_1 (not_1_out, BrEq);
  and and_3 (and_3_out, not_1_out, decoder_1_out1);
  and and_4 (and_4_out, BrLt, or_2_out);
  or or_2 (or_2_out, decoder_1_out4, decoder_1_out6);
  or or_3 (or_3_out, decoder_1_out5, decoder_1_out7);
  and and_5 (and_5_out, or_3_out, not_2_out);
  not not_2 (not_2_out, BrLt);
  and and_6 (and_6_out, comparator_22_eq, comparator_10_eq, comparator_11_eq);
  and and_7 (and_7_out, comparator_10_eq, comparator_12_eq);
  or or_4 (or_4_out, and_2_out, and_3_out, and_4_out, and_5_out);
  and and_8 (and_8_out, comparator_3_eq, or_4_out);
  or or_5 (PCSel, and_8_out, comparator_4_eq, comparator_5_eq);
  Comparator #(.width(7)) comparator_19 (.a(inst[6:0]), .b(7'b0110111), .eq(comparator_19_eq));  // open: gt, lt
  Comparator #(.width(7)) comparator_20 (.a(inst[6:0]), .b(7'b1101111), .eq(comparator_20_eq));  // open: gt, lt
  Comparator #(.width(7)) comparator_21 (.a(inst[6:0]), .b(7'b1100111), .eq(comparator_21_eq));  // open: gt, lt
  or or_6 (RegWEn, comparator_19_eq, comparator_20_eq, comparator_21_eq, comparator_6_eq, comparator_7_eq, comparator_8_eq, comparator_9_eq);
  Comparator #(.width(7)) comparator_22 (.a(inst[31:25]), .b({7{1'b0}}), .eq(comparator_22_eq));  // open: gt, lt
  or or_7 (or_7_out, and_6_out, and_7_out, comparator_13_eq);
  or or_8 (a00, or_7_out, or_9_out, or_1_out);
  Comparator #(.width(7)) comparator_23 (.a(inst[6:0]), .b(7'b0010111), .eq(comparator_23_eq));  // open: gt, lt
  or or_9 (or_9_out, comparator_23_eq, comparator_24_eq, comparator_14_eq);
  Comparator #(.width(7)) comparator_24 (.a(inst[6:0]), .b(7'b1100011), .eq(comparator_24_eq));  // open: gt, lt
  Comparator #(.width(3)) comparator_25 (.a(inst[14:12]), .b(3'b000), .eq(comparator_25_eq));  // open: gt, lt
  and and_9 (a10, comparator_25_eq, comparator_16_eq, comparator_15_eq);
  and and_10 (a12, comparator_25_eq, comparator_17_eq, comparator_15_eq);
  Comparator #(.width(3)) comparator_26 (.a(inst[14:12]), .b(3'b011), .eq(comparator_26_eq));  // open: gt, lt
  and and_11 (a11, comparator_26_eq, comparator_15_eq, comparator_16_eq);
  Comparator #(.width(3)) comparator_27 (.a(inst[14:12]), .b(3'b100), .eq(comparator_27_eq));  // open: gt, lt
  and and_12 (a03, comparator_27_eq, or_11_out);
  Comparator #(.width(3)) comparator_28 (.a(inst[14:12]), .b(3'b001), .eq(comparator_28_eq));  // open: gt, lt
  and and_13 (and_13_out, comparator_28_eq, or_11_out);
  Comparator #(.width(3)) comparator_29 (.a(inst[14:12]), .b(3'b010), .eq(comparator_29_eq));  // open: gt, lt
  and and_14 (a07, comparator_29_eq, or_11_out);
  assign ImmSel = comparator_30_eq ? 3'b101 : 3'bz;  // Controlled_Buffer controlled_buffer_1
  Comparator #(.width(7)) comparator_30 (.a(inst[6:0]), .b(7'b0110011), .eq(comparator_30_eq));  // open: gt, lt
  assign ImmSel = comparator_31_eq ? 3'b001 : 3'bz;  // Controlled_Buffer controlled_buffer_2
  Comparator #(.width(7)) comparator_31 (.a(inst[6:0]), .b(7'b0100011), .eq(comparator_31_eq));  // open: gt, lt
  assign ImmSel = comparator_32_eq ? 3'b010 : 3'bz;  // Controlled_Buffer controlled_buffer_3
  Comparator #(.width(7)) comparator_32 (.a(inst[6:0]), .b(7'b1100011), .eq(comparator_32_eq));  // open: gt, lt
  assign ImmSel = comparator_33_eq ? 3'b011 : 3'bz;  // Controlled_Buffer controlled_buffer_4
  Comparator #(.width(7)) comparator_33 (.a(inst[6:0]), .b(7'b0110111), .eq(comparator_33_eq));  // open: gt, lt
  assign ImmSel = comparator_34_eq ? 3'b011 : 3'bz;  // Controlled_Buffer controlled_buffer_5
  Comparator #(.width(7)) comparator_34 (.a(inst[6:0]), .b(7'b0010111), .eq(comparator_34_eq));  // open: gt, lt
  assign ImmSel = comparator_35_eq ? 3'b100 : 3'bz;  // Controlled_Buffer controlled_buffer_6
  Comparator #(.width(7)) comparator_35 (.a(inst[6:0]), .b(7'b1101111), .eq(comparator_35_eq));  // open: gt, lt
  assign ImmSel = comparator_36_eq ? 3'b110 : 3'bz;  // Controlled_Buffer controlled_buffer_7
  Comparator #(.width(7)) comparator_36 (.a(inst[6:0]), .b(7'b1110011), .eq(comparator_36_eq));  // open: gt, lt
  Comparator #(.width(7)) comparator_37 (.a(inst[6:0]), .b(7'b1100011), .eq(comparator_37_eq));  // open: gt, lt
  Comparator #(.width(3)) comparator_38 (.a(inst[14:12]), .b(3'b110), .eq(comparator_38_eq));  // open: gt, lt
  or or_10 (or_10_out, comparator_38_eq, comparator_39_eq);
  Comparator #(.width(3)) comparator_39 (.a(inst[14:12]), .b(3'b111), .eq(comparator_39_eq));  // open: gt, lt
  Comparator #(.width(7)) comparator_40 (.a(inst[6:0]), .b(7'b0110011), .eq(comparator_40_eq));  // open: gt, lt
  or or_11 (or_11_out, comparator_40_eq, comparator_41_eq);
  Comparator #(.width(7)) comparator_41 (.a(inst[6:0]), .b(7'b0010011), .eq(comparator_41_eq));  // open: gt, lt
  Comparator #(.width(3)) comparator_42 (.a(inst[14:12]), .b(3'b101), .eq(comparator_42_eq));  // open: gt, lt
  and and_15 (a06, comparator_45_eq, and_13_out);
  or or_12 (or_12_out, comparator_30_eq, comparator_31_eq, comparator_32_eq);
  assign ImmSel = not_3_out ? 3'b000 : 3'bz;  // Controlled_Buffer controlled_buffer_8
  or or_13 (or_13_out, or_12_out, comparator_33_eq, or_14_out);
  not not_3 (not_3_out, or_13_out);
  or or_14 (or_14_out, comparator_34_eq, comparator_35_eq, comparator_36_eq);
  and and_16 (BrUn, comparator_37_eq, or_10_out);
  Comparator #(.width(3)) comparator_43 (.a(inst[14:12]), .b(3'b111), .eq(comparator_43_eq));  // open: gt, lt
  and and_17 (a01, comparator_43_eq, or_11_out);
  Comparator #(.width(3)) comparator_44 (.a(inst[14:12]), .b(3'b110), .eq(comparator_44_eq));  // open: gt, lt
  and and_18 (a02, comparator_44_eq, or_11_out);
  and and_19 (and_19_out, comparator_42_eq, or_11_out);
  and and_20 (a04, comparator_45_eq, and_19_out);
  and and_21 (a05, comparator_46_eq, and_19_out);
  Comparator #(.width(7)) comparator_45 (.a(inst[31:25]), .b({7{1'b0}}), .eq(comparator_45_eq));  // open: gt, lt
  Comparator #(.width(7)) comparator_46 (.a(inst[31:25]), .b(7'b0100000), .eq(comparator_46_eq));  // open: gt, lt
  not not_4 (not_4_out, or_15_out);
  or or_15 (or_15_out, a00, or_16_out, or_17_out, or_18_out);
  or or_16 (or_16_out, a01, a02, a03, a04);
  or or_17 (or_17_out, a05, a06, a07, a10);
  or or_18 (or_18_out, a11, a12, a14);
  Comparator #(.width(7)) comparator_47 (.a(inst[6:0]), .b(7'b1100011), .eq(comparator_47_eq));  // open: gt, lt
  or or_19 (ASel, comparator_47_eq, comparator_48_eq, comparator_49_eq);
  Comparator #(.width(7)) comparator_48 (.a(inst[6:0]), .b(7'b0010111), .eq(comparator_48_eq));  // open: gt, lt
  Comparator #(.width(7)) comparator_49 (.a(inst[6:0]), .b(7'b1101111), .eq(comparator_49_eq));  // open: gt, lt
  not not_5 (BSel, comparator_50_eq);
  Comparator #(.width(7)) comparator_50 (.a(inst[6:0]), .b(7'b0110011), .eq(comparator_50_eq));  // open: gt, lt
  or or_20 (or_20_out, a00, not_4_out);
  Comparator #(.width(7)) comparator_51 (.a(inst[6:0]), .b(7'b1110011), .eq(CSRWen));  // open: gt, lt
  Comparator #(.width(3)) comparator_52 (.a(inst[14:12]), .b(3'b001), .eq(comparator_52_eq));  // open: gt, lt
  Comparator #(.width(3)) comparator_53 (.a(inst[14:12]), .b(3'b101), .eq(comparator_53_eq));  // open: gt, lt
  assign ALUSel = or_20_out ? 4'b0000 : 4'bz;  // Controlled_Buffer controlled_buffer_9
  assign ALUSel = a01 ? 4'b0001 : 4'bz;  // Controlled_Buffer controlled_buffer_10
  assign ALUSel = a02 ? 4'b0010 : 4'bz;  // Controlled_Buffer controlled_buffer_11
  assign ALUSel = a03 ? 4'b0011 : 4'bz;  // Controlled_Buffer controlled_buffer_12
  assign ALUSel = a04 ? 4'b0100 : 4'bz;  // Controlled_Buffer controlled_buffer_13
  assign ALUSel = a05 ? 4'b0101 : 4'bz;  // Controlled_Buffer controlled_buffer_14
  assign ALUSel = a06 ? 4'b0110 : 4'bz;  // Controlled_Buffer controlled_buffer_15
  assign ALUSel = a07 ? 4'b0111 : 4'bz;  // Controlled_Buffer controlled_buffer_16
  assign ALUSel = a10 ? 4'b1010 : 4'bz;  // Controlled_Buffer controlled_buffer_17
  assign ALUSel = a11 ? 4'b1011 : 4'bz;  // Controlled_Buffer controlled_buffer_18
  assign ALUSel = a12 ? 4'b1100 : 4'bz;  // Controlled_Buffer controlled_buffer_19
  assign ALUSel = a14 ? 4'b1110 : 4'bz;  // Controlled_Buffer controlled_buffer_20
  // AND_Gate and_22 has open pins: in0=CSRWen, in1=comparator_52_eq, out=open
  and and_23 (CSRSel, CSRWen, comparator_53_eq);
  Comparator #(.width(7)) comparator_54 (.a(inst[6:0]), .b(7'b0100011), .eq(MemRW));  // open: gt, lt
  Comparator #(.width(7)) comparator_55 (.a(inst[6:0]), .b(7'b0000011), .eq(comparator_55_eq));  // open: gt, lt
  Comparator #(.width(7)) comparator_56 (.a(inst[6:0]), .b(7'b1101111), .eq(comparator_56_eq));  // open: gt, lt
  Comparator #(.width(7)) comparator_57 (.a(inst[6:0]), .b(7'b1100111), .eq(comparator_57_eq));  // open: gt, lt
  Comparator #(.width(7)) comparator_58 (.a(inst[6:0]), .b(7'b0100011), .eq(comparator_58_eq));  // open: gt, lt
  Comparator #(.width(3)) comparator_59 (.a(inst[14:12]), .b(3'b000), .eq(comparator_59_eq));  // open: gt, lt
  Comparator #(.width(3)) comparator_60 (.a(inst[14:12]), .b(3'b001), .eq(comparator_60_eq));  // open: gt, lt
  Comparator #(.width(3)) comparator_61 (.a(inst[14:12]), .b(3'b010), .eq(comparator_61_eq));  // open: gt, lt
  Comparator #(.width(7)) comparator_62 (.a(inst[6:0]), .b(7'b0000011), .eq(comparator_62_eq));  // open: gt, lt
  Comparator #(.width(3)) comparator_63 (.a(inst[14:12]), .b(3'b000), .eq(comparator_63_eq));  // open: gt, lt
  Comparator #(.width(3)) comparator_64 (.a(inst[14:12]), .b(3'b001), .eq(comparator_64_eq));  // open: gt, lt
  Comparator #(.width(3)) comparator_65 (.a(inst[14:12]), .b(3'b010), .eq(comparator_65_eq));  // open: gt, lt
  assign WBSel = comparator_55_eq ? 2'b01 : 2'bz;  // Controlled_Buffer controlled_buffer_21
  assign WBSel = or_21_out ? 2'b10 : 2'bz;  // Controlled_Buffer controlled_buffer_22
  or or_21 (or_21_out, comparator_56_eq, comparator_57_eq);
  not not_6 (not_6_out, or_22_out);
  or or_22 (or_22_out, or_21_out, comparator_55_eq);
  assign WSel = and_24_out ? 4'b0001 : 4'bz;  // Controlled_Buffer controlled_buffer_23
  and and_24 (and_24_out, comparator_58_eq, comparator_59_eq);
  assign WSel = and_25_out ? 4'b0011 : 4'bz;  // Controlled_Buffer controlled_buffer_24
  and and_25 (and_25_out, comparator_58_eq, comparator_60_eq);
  assign WSel = and_26_out ? 4'b1111 : 4'bz;  // Controlled_Buffer controlled_buffer_25
  and and_26 (and_26_out, comparator_58_eq, comparator_61_eq);
  assign WSel = not_7_out ? 4'b0000 : 4'bz;  // Controlled_Buffer controlled_buffer_26
  or or_23 (or_23_out, and_24_out, and_25_out, and_26_out);
  not not_7 (not_7_out, or_23_out);
  assign RSel = and_27_out ? 4'b0001 : 4'bz;  // Controlled_Buffer controlled_buffer_27
  and and_27 (and_27_out, comparator_62_eq, comparator_63_eq);
  assign RSel = and_28_out ? 4'b0011 : 4'bz;  // Controlled_Buffer controlled_buffer_28
  and and_28 (and_28_out, comparator_62_eq, comparator_64_eq);
  assign RSel = and_29_out ? 4'b1111 : 4'bz;  // Controlled_Buffer controlled_buffer_29
  and and_29 (and_29_out, comparator_62_eq, comparator_65_eq);
  assign RSel = not_8_out ? 4'b0000 : 4'bz;  // Controlled_Buffer controlled_buffer_30
  or or_24 (or_24_out, and_27_out, and_28_out, and_29_out);
  not not_8 (not_8_out, or_24_out);
  assign WBSel = not_6_out ? 2'b00 : 2'bz;  // Controlled_Buffer controlled_buffer_31

  // Other names for the same wires on the sheet: funct7[6:0] = inst[31:25]; funct10[9:0] = {inst[14:12], inst[31:25]};
  //   funct3[2:0] = inst[14:12]; opcode[6:0] = inst[6:0]

  // Notes on the sheet:
  //   INPUTS to your circuit
  //   DON'T CHANGE THE LOCATIONS OF THE INPUTS AND OUTPUTS!
  //   OUTPUT from your circuit
endmodule
