// Logisim project cpu.circ as structural Verilog: 1 circuit, main circuit cpu
module cpu (
  input  clk,
  input  [31:0] INSTRUCTION,
  input  [31:0] READ_DATA,
  output [31:0] WRITE_ADDRESS,
  output [31:0] PROGRAM_COUNTER,
  output [31:0] ra,
  output [31:0] sp,
  output [31:0] t0,
  output [31:0] t1,
  output [31:0] t2,
  output [31:0] s0,
  output [31:0] s1,
  output [31:0] a0,
  output [31:0] tohost,
  output [3:0] WRITE_ENABLE,
  output [31:0] WRITE_DATA
);

  wire ASel, branch_comp_1_breq, branch_comp_1_brlt, BSel, control_logic_1_brun, control_logic_1_csrsel,
       control_logic_1_csrwen, control_logic_1_regwen, PCSel;
  wire [1:0] WBSel;
  wire [2:0] control_logic_1_immsel;
  wire [3:0] control_logic_1_alusel, RSel;
  wire [31:0] adder_1_out, adder_2_out, controlled_buffer_1_out, imm, INSTRUCTION_t, multiplexer_1_out,
       multiplexer_2_out, multiplexer_3_out, multiplexer_4_out, multiplexer_5_out, multiplexer_6_out,
       regfile_1_read_data_1, register_1_q;

  Adder #(.width(32)) adder_1 (.a(PROGRAM_COUNTER), .b(32'h4), .out(adder_1_out));  // open: cin, cout
  Multiplexer #(.enable("false"), .width(32)) multiplexer_1 (
    .in0(adder_1_out), .in1(WRITE_ADDRESS), .out(multiplexer_1_out), .sel(PCSel));
  Register #(.width(32)) PC (.D(multiplexer_1_out), .clk(clk), .Q(PROGRAM_COUNTER));  // open: en, clr
  Register #(.width(32)) register_1 (.D(PROGRAM_COUNTER), .clk(clk), .Q(register_1_q));  // open: en, clr
  Adder #(.width(32)) adder_2 (.a(register_1_q), .b(32'h4), .out(adder_2_out));  // open: cin, cout
  control_logic control_logic_1 (
    .CSRWen(control_logic_1_csrwen), .WSel(WRITE_ENABLE), .RSel(RSel), .PCSel(PCSel),
    .RegWEn(control_logic_1_regwen), .ImmSel(control_logic_1_immsel), .BrUn(control_logic_1_brun),
    .ASel(ASel), .BSel(BSel), .ALUSel(control_logic_1_alusel), .WBSel(WBSel),
    .CSRSel(control_logic_1_csrsel), .inst(INSTRUCTION_t), .BrEq(branch_comp_1_breq),
    .BrLt(branch_comp_1_brlt));  // open: MemRW
  imm_gen imm_gen_1 (.inst(INSTRUCTION_t), .ImmSel(control_logic_1_immsel), .imm(imm));
  Register #(.width(32)) register_2 (.D(multiplexer_2_out), .clk(clk), .Q(INSTRUCTION_t));  // open: en, clr
  Multiplexer #(.enable("false"), .width(32)) multiplexer_2 (
    .in0(INSTRUCTION), .in1(32'h13), .out(multiplexer_2_out), .sel(PCSel));
  regfile regfile_1 (
    .rs1(INSTRUCTION_t[19:15]), .rs2(INSTRUCTION_t[24:20]), .rd(INSTRUCTION_t[11:7]),
    .Write_Data(multiplexer_6_out), .RegWEn(control_logic_1_regwen), .clk(clk), .ra(ra), .sp(sp), .t0(t0),
    .t1(t1), .t2(t2), .s0(s0), .s1(s1), .a0(a0), .Read_Data_1(regfile_1_read_data_1), .Read_Data_2(WRITE_DATA));
  branch_comp branch_comp_1 (
    .rs1(regfile_1_read_data_1), .rs2(WRITE_DATA), .BrUn(control_logic_1_brun), .BrEq(branch_comp_1_breq),
    .BrLt(branch_comp_1_brlt));
  Multiplexer #(.enable("false"), .width(32)) multiplexer_3 (
    .in0(regfile_1_read_data_1), .in1(register_1_q), .out(multiplexer_3_out), .sel(ASel));
  Multiplexer #(.enable("false"), .width(32)) multiplexer_4 (
    .in0(WRITE_DATA), .in1(imm), .out(multiplexer_4_out), .sel(BSel));
  Multiplexer #(.enable("false"), .width(32)) multiplexer_5 (
    .in0(regfile_1_read_data_1), .in1(imm), .out(multiplexer_5_out), .sel(control_logic_1_csrsel));
  alu alu_1 (.Result(WRITE_ADDRESS), .A(multiplexer_3_out), .B(multiplexer_4_out), .ALUSel(control_logic_1_alusel));
  Multiplexer #(.enable("false"), .select(2), .width(32)) multiplexer_6 (
    .in0(WRITE_ADDRESS), .in1(controlled_buffer_1_out), .in2(adder_2_out), .out(multiplexer_6_out),
    .sel(WBSel));  // open: in3
  csr csr_1 (
    .CSR_address(INSTRUCTION_t[31:20]), .CSR_din(multiplexer_5_out), .CSR_WE(control_logic_1_csrwen),
    .clk(clk), .tohost(tohost));
  assign controlled_buffer_1_out[7:0] = RSel[0] ? READ_DATA[7:0] : 8'bz;  // Controlled_Buffer controlled_buffer_1
  assign controlled_buffer_1_out[15:8] = RSel[1] ? READ_DATA[15:8] : 8'bz;  // Controlled_Buffer controlled_buffer_2
  assign controlled_buffer_1_out[23:16] = RSel[2] ? READ_DATA[23:16] : 8'bz;  // Controlled_Buffer controlled_buffer_3
  assign controlled_buffer_1_out[31:24] = RSel[3] ? READ_DATA[31:24] : 8'bz;  // Controlled_Buffer controlled_buffer_4

  // Other names for the same wires on the sheet: opcode[6:0] = INSTRUCTION_t[6:0]; rd[4:0] = INSTRUCTION_t[11:7];
  //   rs1[4:0] = INSTRUCTION_t[19:15]; rs2[4:0] = INSTRUCTION_t[24:20]; pcJump[31:0] = WRITE_ADDRESS;
  //   WSel[3:0] = WRITE_ENABLE

  // Notes on the sheet:
  //   Output to IMEM
  //   IMEM (do **NOT** move this)
  //   Inputs from IMEM
  //   Inputs/Outputs for testing. Do **NOT** move these.
  //   Outputs To DMEM
  //   DMEM (do **NOT** move this)
  //   Inputs From DMEM
endmodule
