// Logisim project csr.circ as structural Verilog: 1 circuit, main circuit csr
module csr (
  input  [11:0] CSR_address,
  input  [31:0] CSR_din,
  input  CSR_WE,
  input  clk,
  output [31:0] tohost
);

  wire and_1_out, comparator_1_eq;

  Comparator #(.width(12)) comparator_1 (.a(12'h51e), .b(CSR_address), .eq(comparator_1_eq));  // open: gt, lt
  and and_1 (and_1_out, comparator_1_eq, CSR_WE);
  Register #(.width(32)) register_1 (.D(CSR_din), .en(and_1_out), .clk(clk), .Q(tohost));  // open: clr

  // Notes on the sheet:
  //   INPUTS to your circuit
  //   DON'T CHANGE THE LOCATIONS OF THE INPUTS AND OUTPUTS!
  //   OUTPUT from your circuit
endmodule
