// Logisim project imm_gen.circ as structural Verilog: 1 circuit, main circuit imm_gen
module imm_gen (
  input  [31:0] inst,
  input  [2:0] ImmSel,
  output [31:0] imm
);

  wire [11:0] multiplexer_2_out;
  wire [19:0] multiplexer_1_out;
  wire [27:0] multiplexer_3_out;

  Multiplexer #(.enable("false"), .width(20)) multiplexer_1 (
    .in0({20{1'b0}}), .in1({20{1'b1}}), .out(multiplexer_1_out), .sel(inst[31]));
  Multiplexer #(.enable("false"), .width(12)) multiplexer_2 (
    .in0({12{1'b0}}), .in1({12{1'b1}}), .out(multiplexer_2_out), .sel(inst[31]));
  Multiplexer #(.enable("false"), .width(28)) multiplexer_3 (
    .in0({28{1'b0}}), .in1({28{1'b1}}), .out(multiplexer_3_out), .sel(inst[19]));
  Multiplexer #(.enable("false"), .select(3), .width(32)) multiplexer_4 (
    .in0({multiplexer_1_out, inst[31:20]}), .in1({multiplexer_1_out, inst[31:25], inst[11:7]}),
    .in2({multiplexer_1_out, inst[7], inst[30:25], inst[11:8], 1'b0}), .in3({inst[31:12], {12{1'b0}}}),
    .in4({multiplexer_2_out, inst[19:12], inst[20], inst[30:21], 1'b0}), .in5({32{1'b0}}),
    .in6({multiplexer_3_out, inst[18:15]}), .in7({32{1'b0}}), .out(imm), .sel(ImmSel));

  // Notes on the sheet:
  //   INPUTS to your circuit
  //   DON'T CHANGE THE LOCATIONS OF THE INPUTS AND OUTPUTS!
  //   OUTPUT from your circuit
endmodule
