// Logisim project regfile.circ as structural Verilog: 1 circuit, main circuit regfile
module regfile (
  input  [4:0] rs1,
  input  [4:0] rs2,
  input  [4:0] rd,
  input  [31:0] Write_Data,
  input  RegWEn,
  input  clk,
  output [31:0] ra,
  output [31:0] sp,
  output [31:0] t0,
  output [31:0] t1,
  output [31:0] t2,
  output [31:0] s0,
  output [31:0] s1,
  output [31:0] a0,
  output [31:0] Read_Data_1,
  output [31:0] Read_Data_2
);

  wire rda0, rda1, rda2, rda3, rda4, rda5, rda6, rda7, rda8, rda9, rda10, rda11, rda12, rda13, rda14, rda15,
       rda16, rda17, rda18, rda19, rda20, rda21, rda22, rda23, rda24, rda25, rda26, rda27, rda28, rda29,
       rda30, rda31, rdb0, rdb1, rdb2, rdb3, rdb4, rdb5, rdb6, rdb7, rdb8, rdb9, rdb10, rdb11, rdb12, rdb13,
       rdb14, rdb15, rdb16, rdb17, rdb18, rdb19, rdb20, rdb21, rdb22, rdb23, rdb24, rdb25, rdb26, rdb27,
       rdb28, rdb29, rdb30, rdb31, w0, w1, w2, w3, w4, w5, w6, w7, w8, w9, w10, w11, w12, w13, w14, w15, w16,
       w17, w18, w19, w20, w21, w22, w23, w24, w25, w26, w27, w28, w29, w30, w31;
  wire [31:0] register_1_q, register_4_q, register_5_q, register_12_q, register_13_q, register_14_q,
       register_15_q, register_16_q, register_17_q, register_18_q, register_19_q, register_20_q,
       register_21_q, register_22_q, register_23_q, register_24_q, register_25_q, register_26_q,
       register_27_q, register_28_q, register_29_q, register_30_q, register_31_q, register_32_q;

  Decoder #(.enable("false"), .select(5)) decoder_1 (
    .out0(rda0), .out1(rda1), .out2(rda2), .out3(rda3), .out4(rda4), .out5(rda5), .out6(rda6), .out7(rda7),
    .out8(rda8), .out9(rda9), .out10(rda10), .out11(rda11), .out12(rda12), .out13(rda13), .out14(rda14),
    .out15(rda15), .out16(rda16), .out17(rda17), .out18(rda18), .out19(rda19), .out20(rda20), .out21(rda21),
    .out22(rda22), .out23(rda23), .out24(rda24), .out25(rda25), .out26(rda26), .out27(rda27), .out28(rda28),
    .out29(rda29), .out30(rda30), .out31(rda31), .sel(rs1));
  Decoder #(.enable("false"), .select(5)) decoder_2 (
    .out0(rdb0), .out1(rdb1), .out2(rdb2), .out3(rdb3), .out4(rdb4), .out5(rdb5), .out6(rdb6), .out7(rdb7),
    .out8(rdb8), .out9(rdb9), .out10(rdb10), .out11(rdb11), .out12(rdb12), .out13(rdb13), .out14(rdb14),
    .out15(rdb15), .out16(rdb16), .out17(rdb17), .out18(rdb18), .out19(rdb19), .out20(rdb20), .out21(rdb21),
    .out22(rdb22), .out23(rdb23), .out24(rdb24), .out25(rdb25), .out26(rdb26), .out27(rdb27), .out28(rdb28),
    .out29(rdb29), .out30(rdb30), .out31(rdb31), .sel(rs2));
  Decoder #(.select(5)) decoder_3 (
    .out0(w0), .out1(w1), .out2(w2), .out3(w3), .out4(w4), .out5(w5), .out6(w6), .out7(w7), .out8(w8),
    .out9(w9), .out10(w10), .out11(w11), .out12(w12), .out13(w13), .out14(w14), .out15(w15), .out16(w16),
    .out17(w17), .out18(w18), .out19(w19), .out20(w20), .out21(w21), .out22(w22), .out23(w23), .out24(w24),
    .out25(w25), .out26(w26), .out27(w27), .out28(w28), .out29(w29), .out30(w30), .out31(w31), .sel(rd),
    .en(RegWEn));
  Register #(.width(32)) register_1 (.Q(register_1_q));  // open: D, en, clk, clr
  Register #(.width(32)) register_2 (.D(Write_Data), .en(w1), .clk(clk), .Q(ra));  // open: clr
  Register #(.width(32)) register_3 (.D(Write_Data), .en(w2), .clk(clk), .Q(sp));  // open: clr
  Register #(.width(32)) register_4 (.D(Write_Data), .en(w3), .clk(clk), .Q(register_4_q));  // open: clr
  Register #(.width(32)) register_5 (.D(Write_Data), .en(w4), .clk(clk), .Q(register_5_q));  // open: clr
  Register #(.width(32)) register_6 (.D(Write_Data), .en(w5), .clk(clk), .Q(t0));  // open: clr
  Register #(.width(32)) register_7 (.D(Write_Data), .en(w6), .clk(clk), .Q(t1));  // open: clr
  Register #(.width(32)) register_8 (.D(Write_Data), .en(w7), .clk(clk), .Q(t2));  // open: clr
  assign Read_Data_1 = rda0 ? register_1_q : 32'bz;  // Controlled_Buffer controlled_buffer_1
  assign Read_Data_2 = rdb0 ? register_1_q : 32'bz;  // Controlled_Buffer controlled_buffer_2
  assign Read_Data_1 = rda1 ? ra : 32'bz;  // Controlled_Buffer controlled_buffer_3
  assign Read_Data_2 = rdb1 ? ra : 32'bz;  // Controlled_Buffer controlled_buffer_4
  assign Read_Data_1 = rda2 ? sp : 32'bz;  // Controlled_Buffer controlled_buffer_5
  assign Read_Data_2 = rdb2 ? sp : 32'bz;  // Controlled_Buffer controlled_buffer_6
  assign Read_Data_1 = rda3 ? register_4_q : 32'bz;  // Controlled_Buffer controlled_buffer_7
  assign Read_Data_2 = rdb3 ? register_4_q : 32'bz;  // Controlled_Buffer controlled_buffer_8
  assign Read_Data_1 = rda4 ? register_5_q : 32'bz;  // Controlled_Buffer controlled_buffer_9
  assign Read_Data_2 = rdb4 ? register_5_q : 32'bz;  // Controlled_Buffer controlled_buffer_10
  assign Read_Data_1 = rda5 ? t0 : 32'bz;  // Controlled_Buffer controlled_buffer_11
  assign Read_Data_2 = rdb5 ? t0 : 32'bz;  // Controlled_Buffer controlled_buffer_12
  assign Read_Data_1 = rda6 ? t1 : 32'bz;  // Controlled_Buffer controlled_buffer_13
  assign Read_Data_2 = rdb6 ? t1 : 32'bz;  // Controlled_Buffer controlled_buffer_14
  assign Read_Data_1 = rda7 ? t2 : 32'bz;  // Controlled_Buffer controlled_buffer_15
  assign Read_Data_2 = rdb7 ? t2 : 32'bz;  // Controlled_Buffer controlled_buffer_16
  Register #(.width(32)) register_9 (.D(Write_Data), .en(w8), .clk(clk), .Q(s0));  // open: clr
  Register #(.width(32)) register_10 (.D(Write_Data), .en(w9), .clk(clk), .Q(s1));  // open: clr
  Register #(.width(32)) register_11 (.D(Write_Data), .en(w10), .clk(clk), .Q(a0));  // open: clr
  Register #(.width(32)) register_12 (.D(Write_Data), .en(w11), .clk(clk), .Q(register_12_q));  // open: clr
  Register #(.width(32)) register_13 (.D(Write_Data), .en(w12), .clk(clk), .Q(register_13_q));  // open: clr
  Register #(.width(32)) register_14 (.D(Write_Data), .en(w13), .clk(clk), .Q(register_14_q));  // open: clr
  Register #(.width(32)) register_15 (.D(Write_Data), .en(w14), .clk(clk), .Q(register_15_q));  // open: clr
  Register #(.width(32)) register_16 (.D(Write_Data), .en(w15), .clk(clk), .Q(register_16_q));  // open: clr
  assign Read_Data_1 = rda8 ? s0 : 32'bz;  // Controlled_Buffer controlled_buffer_17
  assign Read_Data_2 = rdb8 ? s0 : 32'bz;  // Controlled_Buffer controlled_buffer_18
  assign Read_Data_1 = rda9 ? s1 : 32'bz;  // Controlled_Buffer controlled_buffer_19
  assign Read_Data_2 = rdb9 ? s1 : 32'bz;  // Controlled_Buffer controlled_buffer_20
  assign Read_Data_1 = rda10 ? a0 : 32'bz;  // Controlled_Buffer controlled_buffer_21
  assign Read_Data_2 = rdb10 ? a0 : 32'bz;  // Controlled_Buffer controlled_buffer_22
  assign Read_Data_1 = rda11 ? register_12_q : 32'bz;  // Controlled_Buffer controlled_buffer_23
  assign Read_Data_2 = rdb11 ? register_12_q : 32'bz;  // Controlled_Buffer controlled_buffer_24
  assign Read_Data_1 = rda12 ? register_13_q : 32'bz;  // Controlled_Buffer controlled_buffer_25
  assign Read_Data_2 = rdb12 ? register_13_q : 32'bz;  // Controlled_Buffer controlled_buffer_26
  assign Read_Data_1 = rda13 ? register_14_q : 32'bz;  // Controlled_Buffer controlled_buffer_27
  assign Read_Data_2 = rdb13 ? register_14_q : 32'bz;  // Controlled_Buffer controlled_buffer_28
  assign Read_Data_1 = rda14 ? register_15_q : 32'bz;  // Controlled_Buffer controlled_buffer_29
  assign Read_Data_2 = rdb14 ? register_15_q : 32'bz;  // Controlled_Buffer controlled_buffer_30
  assign Read_Data_1 = rda15 ? register_16_q : 32'bz;  // Controlled_Buffer controlled_buffer_31
  assign Read_Data_2 = rdb15 ? register_16_q : 32'bz;  // Controlled_Buffer controlled_buffer_32
  Register #(.width(32)) register_17 (.D(Write_Data), .en(w16), .clk(clk), .Q(register_17_q));  // open: clr
  Register #(.width(32)) register_18 (.D(Write_Data), .en(w17), .clk(clk), .Q(register_18_q));  // open: clr
  Register #(.width(32)) register_19 (.D(Write_Data), .en(w18), .clk(clk), .Q(register_19_q));  // open: clr
  Register #(.width(32)) register_20 (.D(Write_Data), .en(w19), .clk(clk), .Q(register_20_q));  // open: clr
  Register #(.width(32)) register_21 (.D(Write_Data), .en(w20), .clk(clk), .Q(register_21_q));  // open: clr
  Register #(.width(32)) register_22 (.D(Write_Data), .en(w21), .clk(clk), .Q(register_22_q));  // open: clr
  Register #(.width(32)) register_23 (.D(Write_Data), .en(w22), .clk(clk), .Q(register_23_q));  // open: clr
  Register #(.width(32)) register_24 (.D(Write_Data), .en(w23), .clk(clk), .Q(register_24_q));  // open: clr
  assign Read_Data_1 = rda16 ? register_17_q : 32'bz;  // Controlled_Buffer controlled_buffer_33
  assign Read_Data_1 = rda17 ? register_18_q : 32'bz;  // Controlled_Buffer controlled_buffer_34
  assign Read_Data_1 = rda18 ? register_19_q : 32'bz;  // Controlled_Buffer controlled_buffer_35
  assign Read_Data_1 = rda19 ? register_20_q : 32'bz;  // Controlled_Buffer controlled_buffer_36
  assign Read_Data_1 = rda20 ? register_21_q : 32'bz;  // Controlled_Buffer controlled_buffer_37
  assign Read_Data_1 = rda21 ? register_22_q : 32'bz;  // Controlled_Buffer controlled_buffer_38
  assign Read_Data_1 = rda22 ? register_23_q : 32'bz;  // Controlled_Buffer controlled_buffer_39
  assign Read_Data_1 = rda23 ? register_24_q : 32'bz;  // Controlled_Buffer controlled_buffer_40
  assign Read_Data_2 = rdb16 ? register_17_q : 32'bz;  // Controlled_Buffer controlled_buffer_41
  assign Read_Data_2 = rdb17 ? register_18_q : 32'bz;  // Controlled_Buffer controlled_buffer_42
  assign Read_Data_2 = rdb18 ? register_19_q : 32'bz;  // Controlled_Buffer controlled_buffer_43
  assign Read_Data_2 = rdb19 ? register_20_q : 32'bz;  // Controlled_Buffer controlled_buffer_44
  assign Read_Data_2 = rdb20 ? register_21_q : 32'bz;  // Controlled_Buffer controlled_buffer_45
  assign Read_Data_2 = rdb21 ? register_22_q : 32'bz;  // Controlled_Buffer controlled_buffer_46
  assign Read_Data_2 = rdb22 ? register_23_q : 32'bz;  // Controlled_Buffer controlled_buffer_47
  assign Read_Data_2 = rdb23 ? register_24_q : 32'bz;  // Controlled_Buffer controlled_buffer_48
  Register #(.width(32)) register_25 (.D(Write_Data), .en(w24), .clk(clk), .Q(register_25_q));  // open: clr
  Register #(.width(32)) register_26 (.D(Write_Data), .en(w25), .clk(clk), .Q(register_26_q));  // open: clr
  Register #(.width(32)) register_27 (.D(Write_Data), .en(w26), .clk(clk), .Q(register_27_q));  // open: clr
  Register #(.width(32)) register_28 (.D(Write_Data), .en(w27), .clk(clk), .Q(register_28_q));  // open: clr
  Register #(.width(32)) register_29 (.D(Write_Data), .en(w28), .clk(clk), .Q(register_29_q));  // open: clr
  Register #(.width(32)) register_30 (.D(Write_Data), .en(w29), .clk(clk), .Q(register_30_q));  // open: clr
  Register #(.width(32)) register_31 (.D(Write_Data), .en(w30), .clk(clk), .Q(register_31_q));  // open: clr
  Register #(.width(32)) register_32 (.D(Write_Data), .en(w31), .clk(clk), .Q(register_32_q));  // open: clr
  assign Read_Data_1 = rda24 ? register_25_q : 32'bz;  // Controlled_Buffer controlled_buffer_49
  assign Read_Data_2 = rdb24 ? register_25_q : 32'bz;  // Controlled_Buffer controlled_buffer_50
  assign Read_Data_1 = rda25 ? register_26_q : 32'bz;  // Controlled_Buffer controlled_buffer_51
  assign Read_Data_2 = rdb25 ? register_26_q : 32'bz;  // Controlled_Buffer controlled_buffer_52
  assign Read_Data_1 = rda26 ? register_27_q : 32'bz;  // Controlled_Buffer controlled_buffer_53
  assign Read_Data_2 = rdb26 ? register_27_q : 32'bz;  // Controlled_Buffer controlled_buffer_54
  assign Read_Data_1 = rda27 ? register_28_q : 32'bz;  // Controlled_Buffer controlled_buffer_55
  assign Read_Data_2 = rdb27 ? register_28_q : 32'bz;  // Controlled_Buffer controlled_buffer_56
  assign Read_Data_1 = rda28 ? register_29_q : 32'bz;  // Controlled_Buffer controlled_buffer_57
  assign Read_Data_2 = rdb28 ? register_29_q : 32'bz;  // Controlled_Buffer controlled_buffer_58
  assign Read_Data_1 = rda29 ? register_30_q : 32'bz;  // Controlled_Buffer controlled_buffer_59
  assign Read_Data_2 = rdb29 ? register_30_q : 32'bz;  // Controlled_Buffer controlled_buffer_60
  assign Read_Data_1 = rda30 ? register_31_q : 32'bz;  // Controlled_Buffer controlled_buffer_61
  assign Read_Data_2 = rdb30 ? register_31_q : 32'bz;  // Controlled_Buffer controlled_buffer_62
  assign Read_Data_1 = rda31 ? register_32_q : 32'bz;  // Controlled_Buffer controlled_buffer_63
  assign Read_Data_2 = rdb31 ? register_32_q : 32'bz;  // Controlled_Buffer controlled_buffer_64

  // Other names for the same wires on the sheet: read_reg1[4:0] = rs1; read_reg2[4:0] = rs2; write_en = RegWEn;
  //   write_reg[4:0] = rd

  // Notes on the sheet:
  //   INPUTS to your circuit
  //   DON'T CHANGE THE LOCATIONS OF THE INPUTS AND OUTPUTS!
  //   These are DEBUG/TEST outputs from your circuit.
  //   OUTPUTS from your circuit
endmodule
